// Logisim project Circuit simulation.circ as structural Verilog
module _10_bit_Register_File (
  input  [9:0] Data,
  input  Read_Write,
  input  [1:0] RS,
  input  [1:0] RD,
  input  [1:0] RT,
  input  Clock,
  output [9:0] Data_Output_1,
  output [9:0] Data_Output_2
);

  wire decoder_1_out0, decoder_1_out1, decoder_1_out2, decoder_1_out3;
  wire [9:0] register_1_q, register_2_q, register_3_q, register_4_q;

  Decoder #(.select(2)) decoder_1 (
    .out0(decoder_1_out0), .out1(decoder_1_out1), .out2(decoder_1_out2), .out3(decoder_1_out3), .sel(RD),
    .en(Read_Write));
  Register #(.width(10)) register_1 (.D(Data), .en(decoder_1_out0), .Q(register_1_q), .clk(Clock));  // open: clr
  Register #(.width(10)) register_2 (.D(Data), .en(decoder_1_out1), .Q(register_2_q), .clk(Clock));  // open: clr
  Register #(.width(10)) register_3 (.D(Data), .en(decoder_1_out2), .Q(register_3_q), .clk(Clock));  // open: clr
  Register #(.width(10)) register_4 (.D(Data), .en(decoder_1_out3), .Q(register_4_q), .clk(Clock));  // open: clr
  Multiplexer #(.select(2), .width(10), .enable("false")) multiplexer_1 (
    .in0(register_1_q), .in1(register_2_q), .in2(register_3_q), .in3(register_4_q), .out(Data_Output_1),
    .sel(RS));
  Multiplexer #(.select(2), .width(10), .enable("false")) multiplexer_2 (
    .in0(register_1_q), .in1(register_2_q), .in2(register_3_q), .in3(register_4_q), .out(Data_Output_2),
    .sel(RT));
endmodule

module ALU (
  input  [9:0] B,
  input  [9:0] A,
  input  Cin,
  input  [3:0] SELECT,
  output [9:0] Output
);

  wire [9:0] adder_1_out, adder_2_out, adder_3_out, adder_4_out, adder_5_out, and_1_out, and_2_out,
       comparator_1_out_6, nand_1_out, nor_1_out, or_1_out, shifter_1_out, shifter_2_out, subtractor_1_out,
       subtractor_2_out, xor_1_out;

  Adder #(.width(10)) adder_1 (.a(A), .b(B), .out(adder_1_out), .cin(Cin));  // open: cout
  Subtractor #(.width(10)) subtractor_1 (.a(A), .b(B), .out(subtractor_1_out), .bin(Cin));  // open: bout
  assign and_1_out = A & B;  // AND_Gate and_1, 10 bits wide
  assign or_1_out = A | B;  // OR_Gate or_1, 10 bits wide
  assign xor_1_out = A ^ B;  // XOR_Gate xor_1, 10 bits wide
  Comparator comparator_1 (.B(B), .A(A), .out_6(comparator_1_out_6));  // open: in_1, in_4, in_5
  assign nor_1_out = ~(A | B);  // NOR_Gate nor_1, 10 bits wide
  assign nand_1_out = ~(A & B);  // NAND_Gate nand_1, 10 bits wide
  Adder #(.width(10)) adder_2 (.a(A), .b(B), .out(adder_2_out), .cin(Cin));  // open: cout
  Subtractor #(.width(10)) subtractor_2 (.a(A), .b(B), .out(subtractor_2_out), .bin(Cin));  // open: bout
  Shifter #(.width(10)) shifter_1 (.in(A), .\dist (B[3:0]), .out(shifter_1_out));
  Shifter #(.width(10), .shift("lr")) shifter_2 (.in(A), .\dist (B[3:0]), .out(shifter_2_out));
  assign and_2_out = A & B;  // AND_Gate and_2, 10 bits wide
  Adder #(.width(10)) adder_3 (.a(A), .b(B), .out(adder_3_out));  // open: cin, cout
  Adder #(.width(10)) adder_4 (.a(A), .b(B), .out(adder_4_out));  // open: cin, cout
  Adder #(.width(10)) adder_5 (.a({10{1'b0}}), .b(B), .out(adder_5_out));  // open: cin, cout
  Multiplexer #(.select(4), .width(10), .enable("false")) multiplexer_1 (
    .in0(adder_1_out), .in1(subtractor_1_out), .in2(and_1_out), .in3(or_1_out), .in4(xor_1_out),
    .in5(comparator_1_out_6), .in6(nor_1_out), .in7(nand_1_out), .in8(adder_2_out), .in9(subtractor_2_out),
    .in10(shifter_1_out), .in11(shifter_2_out), .in12(adder_3_out), .in13(adder_4_out), .in14(adder_5_out),
    .in15(and_2_out), .out(Output), .sel(SELECT));
endmodule

module Pipeline (
  input  _1,
  input  _2,
  input  _3,
  input  _4,
  input  _5,
  input  _6,
  input  _7,
  input  _8,
  input  _9,
  input  _10,
  input  _11,
  input  _12,
  input  _13,
  input  _14,
  input  _15,
  input  _16,
  input  _17,
  input  _18,
  input  _19,
  input  _20,
  input  _21,
  input  _22,
  input  _23,
  input  _24,
  input  Enabler,
  input  Clock,
  output _1_2,
  output _2_2,
  output _3_2,
  output _4_2,
  output _5_2,
  output _6_2,
  output _7_2,
  output _8_2,
  output _9_2,
  output _10_2,
  output _11_2,
  output _12_2,
  output _13_2,
  output _14_2,
  output _15_2,
  output _16_2,
  output _17_2,
  output _18_2,
  output _19_2,
  output _20_2,
  output _21_2,
  output _22_2,
  output _23_2,
  output _24_2
);

  Register #(.width(1)) register_1 (.D(_1), .en(Enabler), .Q(_1_2), .clk(Clock));  // open: clr
  Register #(.width(1)) register_2 (.D(_2), .en(Enabler), .Q(_2_2), .clk(Clock));  // open: clr
  Register #(.width(1)) register_3 (.D(_3), .en(Enabler), .Q(_3_2), .clk(Clock));  // open: clr
  Register #(.width(1)) register_4 (.D(_4), .en(Enabler), .Q(_4_2), .clk(Clock));  // open: clr
  Register #(.width(1)) register_5 (.D(_5), .en(Enabler), .Q(_5_2), .clk(Clock));  // open: clr
  Register #(.width(1)) register_6 (.D(_6), .en(Enabler), .Q(_6_2), .clk(Clock));  // open: clr
  Register #(.width(1)) register_7 (.D(_7), .en(Enabler), .Q(_7_2), .clk(Clock));  // open: clr
  Register #(.width(1)) register_8 (.D(_8), .en(Enabler), .Q(_8_2), .clk(Clock));  // open: clr
  Register #(.width(1)) register_9 (.D(_9), .en(Enabler), .Q(_9_2), .clk(Clock));  // open: clr
  Register #(.width(1)) register_10 (.D(_10), .en(Enabler), .Q(_10_2), .clk(Clock));  // open: clr
  Register #(.width(1)) register_11 (.D(_11), .en(Enabler), .Q(_11_2), .clk(Clock));  // open: clr
  Register #(.width(1)) register_12 (.D(_12), .en(Enabler), .Q(_12_2), .clk(Clock));  // open: clr
  Register #(.width(1)) register_13 (.D(_13), .en(Enabler), .Q(_13_2), .clk(Clock));  // open: clr
  Register #(.width(1)) register_14 (.D(_14), .en(Enabler), .Q(_14_2), .clk(Clock));  // open: clr
  Register #(.width(1)) register_15 (.D(_15), .en(Enabler), .Q(_15_2), .clk(Clock));  // open: clr
  Register #(.width(1)) register_16 (.D(_16), .en(Enabler), .Q(_16_2), .clk(Clock));  // open: clr
  Register #(.width(1)) register_17 (.D(_17), .en(Enabler), .Q(_17_2), .clk(Clock));  // open: clr
  Register #(.width(1)) register_18 (.D(_18), .en(Enabler), .Q(_18_2), .clk(Clock));  // open: clr
  Register #(.width(1)) register_19 (.D(_19), .en(Enabler), .Q(_19_2), .clk(Clock));  // open: clr
  Register #(.width(1)) register_20 (.D(_20), .en(Enabler), .Q(_20_2), .clk(Clock));  // open: clr
  Register #(.width(1)) register_21 (.D(_21), .en(Enabler), .Q(_21_2), .clk(Clock));  // open: clr
  Register #(.width(1)) register_22 (.D(_22), .en(Enabler), .Q(_22_2), .clk(Clock));  // open: clr
  Register #(.width(1)) register_23 (.D(_23), .en(Enabler), .Q(_23_2), .clk(Clock));  // open: clr
  Register #(.width(1)) register_24 (.D(_24), .en(Enabler), .Q(_24_2), .clk(Clock));  // open: clr
endmodule

module _10_bit_Processor (
  input  [9:0] in_1
);

  wire AluSrc, Clock, MemRead, MemToReg, MemWrite, RegDst, RegWrite;
  wire [1:0] multiplexer_1_out;
  wire [3:0] OpCode;
  wire [5:0] rom_1_data;
  wire [9:0] adder_1_out, alu_1_output, bit_extender_1_out, multiplexer_2_out, multiplexer_3_out,
       n10_bit_register_file_1_data_output_1, n10_bit_register_file_1_data_output_2, ram_1_data, register_1_q;

  Register #(.width(10)) register_1 (.D(adder_1_out), .en(1'b1), .Q(register_1_q), .clk(Clock));  // open: clr
  Control_Unit control_unit_1 (
    .in_1(OpCode), .RegDst(RegDst), .AluSrc(AluSrc), .RegWrite(RegWrite), .MemRead(MemRead),
    .MemToReg(MemToReg), .MemWrite(MemWrite));
  Adder #(.width(10)) adder_1 (.a(in_1), .b(register_1_q), .out(adder_1_out));  // open: cin, cout
  ROM #(.addrWidth(10), .dataWidth(10)) rom_1 (.addr(register_1_q), .data({OpCode, rom_1_data}));  // open: sel
  Button button_1 (.out(Clock));
  assign bit_extender_1_out = {{8{1'b0}}, rom_1_data[1:0]};  // Bit_Extender bit_extender_1
  Multiplexer #(.width(2), .enable("false")) multiplexer_1 (
    .in0(rom_1_data[1:0]), .in1(rom_1_data[3:2]), .out(multiplexer_1_out), .sel(RegDst));
  _10_bit_Register_File u_10_bit_register_file_1 (
    .Data(multiplexer_3_out), .Read_Write(RegWrite), .RS(rom_1_data[5:4]), .RD(multiplexer_1_out),
    .RT(rom_1_data[3:2]), .Clock(Clock), .Data_Output_1(n10_bit_register_file_1_data_output_1),
    .Data_Output_2(n10_bit_register_file_1_data_output_2));
  Multiplexer #(.width(10), .enable("false")) multiplexer_2 (
    .in0(n10_bit_register_file_1_data_output_2), .in1(bit_extender_1_out), .out(multiplexer_2_out),
    .sel(AluSrc));
  ALU alu_1 (
    .B(multiplexer_2_out), .A(n10_bit_register_file_1_data_output_1), .Cin(1'b0), .Output(alu_1_output),
    .SELECT(OpCode));
  RAM #(.addrWidth(10), .dataWidth(10), .bus("separate")) ram_1 (
    .addr(alu_1_output), .din(n10_bit_register_file_1_data_output_2), .data(ram_1_data), .str(MemWrite),
    .clk(Clock), .ld(MemRead));  // open: sel, clr
  Multiplexer #(.width(10), .enable("false")) multiplexer_3 (
    .in0(alu_1_output), .in1(ram_1_data), .out(multiplexer_3_out), .sel(MemToReg));

  // Notes on the sheet:
  //   contents of rom_1 (hex, n*v repeats v):
  //   0 330 371 4*0 330
endmodule

module Control_Unit (
  input  [3:0] in_1,
  output RegDst,
  output AluSrc,
  output RegWrite,
  output MemRead,
  output MemToReg,
  output MemWrite
);

  wire not_1_out, not_2_out, not_3_out, not_4_out, not_5_out, not_6_out;

  not not_1 (not_1_out, in_1[3]);
  not not_2 (not_2_out, in_1[2]);
  not not_3 (not_3_out, in_1[0]);
  not not_4 (not_4_out, in_1[1]);
  not not_5 (not_5_out, in_1[0]);
  not not_6 (not_6_out, in_1[1]);
  or or_1 (RegWrite, not_1_out, not_2_out, not_3_out, in_1[1]);
  and and_1 (MemRead, in_1[3], in_1[2], not_4_out, not_5_out);
  and and_2 (MemWrite, in_1[3], in_1[2], in_1[0], not_6_out);

  assign AluSrc = in_1[3];
  assign MemToReg = MemRead;
  assign RegDst = in_1[3];
endmodule

module Comparator (
  input  [2:0] in_1,
  input  [9:0] B,
  input  [9:0] A,
  input  [2:0] in_4,
  input  [2:0] in_5,
  output [9:0] out_6
);

  wire [2:0] comparator_1_eq, multiplexer_1_out;

  Comparator_part #(.width(10)) comparator_1 (
    .a(A), .b(B), .gt(comparator_1_eq[1]), .eq(comparator_1_eq[0]), .lt(comparator_1_eq[2]));
  Multiplexer #(.select(3), .width(3), .enable("false")) multiplexer_1 (
    .in1(in_1), .in2(in_4), .in4(in_5), .out(multiplexer_1_out), .sel(comparator_1_eq));  // open: in0, in3, in5, in6, in7
  assign out_6 = {{7{1'b0}}, multiplexer_1_out};  // Bit_Extender bit_extender_1
endmodule
